# Fritzing sketch programmator-esp32-cam (saved by Fritzing 1.0.2b)
breadboards: 1

parts:
  ESP32-CAM1 = ESP32-CAM_tve  # not connected
  R1 = Resistor [tolerance=±5% power=0.25W resistance=10k package=THT]  # not connected
  battery1 = Battery3AAA [part_number=001 package=Pack-tve]  # not connected
  S3 = Square Pushbutton  # not connected
  S4 = Momentary Switch [package=ksa_sealed_tac_switch]  # not connected
  USB_UART1 = USB-TTL UART

nets:
  N1: USB_UART1.pin1, USB_UART1.pin2, USB_UART1.pin3
  N2: USB_UART1.pin12, USB_UART1.pin13, USB_UART1.pin14

custom parts:
  ESP32-CAM_tve: The ESP32-CAM has a very competitive small-size camera module that can operate independently as a minimum system with a footprint of only 27*40.5*4.5mm and a deep sleep current of up to 6mA.
  Battery3AAA: Блок 3 элементов питания AAA по 1.5В
  USB-TTL UART: USB programmer interface incorporating Silicon Labs CP2102 UART
